# Fritzing sketch Temperature (saved by Fritzing 0.9.3b)
circuit board: 8.46667cm x 5.64444cm
breadboards: 1

parts:
  Part3 = Arduino Uno (Rev3)
  U1 = LCD-16X2 [package=lcd-16x2_nosilk]
  R1 = Resistor [tolerance=±5% power=0.25 resistance=1k package=THT]
  Q2 = TRANSISTOR_NPN [package=to-92]
  D3 = Diode [package=diode-hv]
  VCC1 = Battery block 9V
  RY2 = srd-05vdc-sl-c
  M2 = DC Motor [voltage_(max)=6V voltage_(min)=3V]
  Q4 = TRANSISTOR_NPN [package=to-92]
  R3 = Resistor [tolerance=±5% resistance=1k package="0603 [SMD]"]
  U2 = Optocoupler [package=THT]  # not connected
  DHT1 = DHT11 Humitidy and Temperature Sensor
  R4 = Resistor [tolerance=±5% resistance=1k package="0603 [SMD]"]
  R5 = Resistor [tolerance=±5% resistance=330 package="0603 [SMD]"]
  LED1 = LED - 5mm [color="Red (633nm)" package="5 mm [THT]"]
  R9 = Resistor [tolerance=±5% resistance=330 package="0603 [SMD]"]

nets:
  N1: Part3.A0, DHT1.DATA
  N2: Part3.D11_PWM/MOSI, Part3.D3_PWM, U1.E
  N3: Part3.D12/MISO, Part3.D2, U1.RS
  N4: Part3.D13/SCK, R1.Pin_1
  N5: Part3.D4, U1.DB4
  N6: Part3.D5_PWM, U1.DB5
  N7: Part3.D6_PWM, U1.DB6
  N8: Part3.D7, U1.DB7
  VDD: Part3.5V, U1.VDD, Q2.C, D3.C, RY2.pin_4, DHT1.VDD
  GND: Part3.GND, U1.VSS, U1.A, VCC1.-, RY2.pin_5, Q4.E, DHT1.GND, R4.Pin_1, R5.Pin_0, LED1.cathode, R9.Pin_0
  N9: U1.VO, R4.Pin_0
  N10: U1.K, R9.Pin_1
  N11: R1.Pin_0, Q2.B
  N12: D3.A, RY2.pin_1, Q4.C
  N13: VCC1.+, M2.pin_2
  N14: RY2.pin_2, M2.pin_1
  N15: Q4.B, R3.Pin_0
  N16: R5.Pin_1, LED1.anode

custom parts:
  DHT11 Humitidy and Temperature Sensor: DHT11 Humidity and Temperature Sensor

// code stored in the sketch: Temperature.ino
#include <LiquidCrystal.h>
LiquidCrystal lcd(2,3,4,5,6,7);
float Temp;
void setup() {
  lcd.begin(16,2);
  lcd.print("Temp = ");
  pinMode(13, OUTPUT);
}

void loop() {
  Temp = 100 * (float)analogRead(A0) * 5 / 1023;
  lcd.setCursor(10,0);
  lcd.print(Temp);
  if(Temp > 40){
    digitalWrite(13, HIGH);
    lcd.setCursor(0,1);
    lcd.print("Overheating");
  }
  else if(Temp < 30){
    digitalWrite(13, LOW);
    lcd.setCursor(0,1);
    lcd.print("Normal     ");
  }
}
